# Fritzing sketch RC Car Wireless Controller (saved by Fritzing 0.9.4)
circuit board: 13cm x 6.6cm

parts:
  Arduino_Nano = Arduino Nano (Rev3.0)
  nRF24L01+ = NRF24L01+ Breakout Board
  Joystick_2 = KY-023 Dual Axis Joystick Module [package="Breakout board"]
  Joystick_1 = KY-023 Dual Axis Joystick Module [package="Breakout board"]
  Battery_(9V) = Battery block 9V
  Switch = SWITCH-SPST-2 [package=switch-spst-vertical]
  Capacitor_(optional) = Capacitor Polarized [package=cpol-radial-10uf-25v]

nets:
  GND: Arduino_Nano.GND, nRF24L01+.GND, Joystick_2.GND, Joystick_1.GND, Battery_(9V).-, Capacitor_(optional).-
  N1: Arduino_Nano.D2, Joystick_1.SW
  N2: Arduino_Nano.D3, Joystick_2.SW
  N3: Arduino_Nano.D7, nRF24L01+.CE
  N4: Arduino_Nano.D8, nRF24L01+.CS
  N5: Arduino_Nano.D11/MOSI, nRF24L01+.MOSI
  N6: Arduino_Nano.D12/MISO, nRF24L01+.MISO
  N7: Arduino_Nano.VIN, Switch.P
  +5V: Arduino_Nano.5V, Joystick_2.+5V, Joystick_1.+5V
  N8: Arduino_Nano.A3, Joystick_2.VRy
  N9: Arduino_Nano.A2, Joystick_2.VRx
  N10: Arduino_Nano.A1, Joystick_1.VRy
  N11: Arduino_Nano.A0, Joystick_1.VRx
  3V3: Arduino_Nano.3V3, nRF24L01+.VCC, Capacitor_(optional).+
  N12: Arduino_Nano.D13/SCK, nRF24L01+.SCK
  N13: Battery_(9V).+, Switch.O

notes:
  PCB design by Devin Namaky

// code stored in the sketch: RC Car Wireless Controller (Namaky).ino
// Uses an Arduino NANO with two analog joysticks (right and left). Sends to nRF24L01 on the car being controlled

//----------------DEFINITIONS AND LIBRARIES---------------------//
#include <SPI.h>
#include <nRF24L01.h>
#include <RF24.h>
RF24 radio(7, 8); // CE, CSN
const byte address[6] = "00001";

struct Data_Package {   // Create a single data package to be sent over wireless
  byte joystick1xAxisBytes;
  byte joystick1yAxisBytes;
  byte joystick2xAxisBytes;
  byte joystick2yAxisBytes;
  };
Data_Package data; // Creates a variable "data" with the above structure of bytes
//------------------------------------------------------//

//----------------------SETUP---------------------------//
void setup() {
  Serial.begin(9600);
  radio.begin();
  radio.openWritingPipe(address);
  radio.setAutoAck(false);
  radio.setDataRate(RF24_250KBPS);
  radio.setPALevel(RF24_PA_LOW);
  radio.stopListening();
  resetData();
}
//------------------------------------------------------//

//------------------MAIN LOOP------------------------//
void loop() {
  data.joystick1xAxisBytes = map(analogRead(A0), 0, 1023, 0, 255); // Read Joystick 1 X-axis and map to bytes
  data.joystick1yAxisBytes = map(analogRead(A1), 0, 1023, 0, 255); // Read Joystick 1 Y-axis and map to bytes
  data.joystick2xAxisBytes = map(analogRead(A2), 0, 1023, 0, 255); // Read Joystick 2 X-axis and map to bytes
  data.joystick2yAxisBytes = map(analogRead(A3), 0, 1023, 0, 255); // Read Joystick 2 Y-axis and map to bytes
  radio.write(&data, sizeof(Data_Package));   // Send the data package to the receiver

}
//------------------------------------------------------//

//----------------OTHER COMMAND DEFINITIONS--------------//
void resetData() {  //resets joystick values to neutral
  data.joystick1xAxisBytes = 127;
  data.joystick1yAxisBytes = 127;
  data.joystick2xAxisBytes = 127;
  data.joystick2yAxisBytes = 127;
  }
  //------------------------------------------------------//
