# Fritzing sketch RC_Car_SS PCB (saved by Fritzing 0.9.4)
circuit board: 4.26368cm x 6.50677cm

parts:
  Motor = Screw terminal - 2 pins [package=THT]
  Servo = Dagu DGServo 9g header (male) [package=THT]
  Ada_Btn = Adafruit Push-button Power Switch Breakout [package=THT]
  Arduino_Nano = Arduino Nano (Rev3.0)
  NRF24L01 = nRF24L01 [package=module]
  TB6612FNG = Motor Driver 1A Dual TB6612FNG
  5-6V_From_Step = Screw terminal - 2 pins [package=THT]
  From_Batt = Screw terminal - 2 pins [package=THT]
  To_Step = Screw terminal - 2 pins [package=THT]

nets:
  N1: Motor.pin1, TB6612FNG.A02
  N2: Motor.pin2, TB6612FNG.A01
  GND: Servo.gnd, Arduino_Nano.GND, 5-6V_From_Step.pin1
  VCC: Servo.Vcc, Arduino_Nano.VIN, TB6612FNG.VM, 5-6V_From_Step.pin2
  N3: Servo.pulse, Arduino_Nano.D5
  N4: Ada_Btn.IN, From_Batt.pin2
  N5: Ada_Btn.OUT, To_Step.pin2
  N6: Ada_Btn.GND, From_Batt.pin1, To_Step.pin1
  N7: Arduino_Nano.D6, TB6612FNG.PWMA
  N8: Arduino_Nano.D7, TB6612FNG.AIN2
  N9: Arduino_Nano.D8, TB6612FNG.AIN1
  N10: Arduino_Nano.D9, NRF24L01.CSN
  N11: Arduino_Nano.D10, NRF24L01.CE
  N12: Arduino_Nano.D11/MOSI, NRF24L01.MOSI
  N13: Arduino_Nano.D12/MISO, NRF24L01.MISO
  5V: Arduino_Nano.5V, TB6612FNG.VCC, TB6612FNG.STBY
  3V3: Arduino_Nano.3V3, NRF24L01.VCC
  N14: Arduino_Nano.D13/SCK, NRF24L01.SCK
  GND_2: NRF24L01.GND, TB6612FNG.GND

notes:
  Wireless Motor Control 5-6V
  RC_Car_SS PCB by Devin Namaky 2020
  www.devinnamaky.com
  github.com/DrNebin/RC_Car
  RC_Car_SS

custom parts:
  nRF24L01: nRF24L01 module
