# Fritzing sketch RC Rebuild (saved by Fritzing 0.9.4)
circuit board: 4.33587cm x 5.07775cm

parts:
  TB6612FNG = Motor Driver 1A Dual TB6612FNG
  XIAXO = seeeduino-xiao
  Motor_B = Screw terminal - 2 pins [package=THT]
  Motor_A = Screw terminal - 2 pins [package=THT]
  Power = Screw terminal - 2 pins [package=THT]
  NRF24L01_WiFi = nRF24L01 [package=module]

nets:
  N1: TB6612FNG.B01, Motor_B.pin2
  N2: TB6612FNG.B02, Motor_B.pin1
  N3: TB6612FNG.A02, Motor_A.pin1
  N4: TB6612FNG.A01, Motor_A.pin2
  GND: TB6612FNG.GND, XIAXO.GND, Power.pin1, NRF24L01_WiFi.GND
  VCC: TB6612FNG.VCC, TB6612FNG.VM, TB6612FNG.STBY, XIAXO.5V, Power.pin2
  N5: TB6612FNG.PWMA, XIAXO.D1
  N6: TB6612FNG.AIN2, XIAXO.D0
  N7: TB6612FNG.AIN1, XIAXO.D2
  N8: TB6612FNG.BIN1, XIAXO.D3
  N9: TB6612FNG.BIN2, XIAXO.D4
  N10: TB6612FNG.PWMB, XIAXO.D5
  N11: XIAXO.D6, NRF24L01_WiFi.CE
  N12: XIAXO.D7, NRF24L01_WiFi.CSN
  N13: XIAXO.D8, NRF24L01_WiFi.SCK
  N14: XIAXO.D9, NRF24L01_WiFi.MISO
  N15: XIAXO.D10, NRF24L01_WiFi.MOSI
  3V3: XIAXO.3V3, NRF24L01_WiFi.VCC

notes:
  Wireless Motor Control 3.3-5V
  PCB by Devin Namaky
  2020
  Seeeduino
  Motor Driver

custom parts:
  seeeduino-xiao: Seeeduino XIAO processor board.
  nRF24L01: nRF24L01 module
