# Fritzing sketch RC_Controller_v2 (saved by Fritzing 0.9.4)
circuit board: 9.81194cm x 5.78554cm
breadboards: 1

parts:
  3V_Itsy_Bitsy_32u4_w_Lipo_Backpack = Itsy Bitsy 32u4 3V @ 8MHz [part_number="Adafruit 3675"]
  Right_Stick_COM-09032 = Thumb Joystick [package=joystick]
  Left_Stick_COM-09032 = Thumb Joystick [package=joystick]
  Power_Switch = Toggle Switch [package=THT]
  100_uF_Capacitor_(Optional) = Capacitor Polarized [package=cpol-radial-10uf-25v]
  From_Batt = Screw terminal - 2 pins [package=THT]
  nRF24L01+ = NRF24L01+ Breakout Board

nets:
  GND: 3V_Itsy_Bitsy_32u4_w_Lipo_Backpack.GND, Right_Stick_COM-09032.SEL-, Right_Stick_COM-09032.H-, Right_Stick_COM-09032.V-, Left_Stick_COM-09032.SEL-, Left_Stick_COM-09032.H-, Left_Stick_COM-09032.V-, 100_uF_Capacitor_(Optional).-, nRF24L01+.GND
  N1: 3V_Itsy_Bitsy_32u4_w_Lipo_Backpack.D13, nRF24L01+.CS
  N2: 3V_Itsy_Bitsy_32u4_w_Lipo_Backpack.D12, nRF24L01+.CE
  N3: 3V_Itsy_Bitsy_32u4_w_Lipo_Backpack.D11, Right_Stick_COM-09032.SEL+
  N4: 3V_Itsy_Bitsy_32u4_w_Lipo_Backpack.D10, Left_Stick_COM-09032.SEL+
  N5: 3V_Itsy_Bitsy_32u4_w_Lipo_Backpack.MISO, nRF24L01+.MISO
  N6: 3V_Itsy_Bitsy_32u4_w_Lipo_Backpack.MOSI, nRF24L01+.MOSI
  N7: 3V_Itsy_Bitsy_32u4_w_Lipo_Backpack.SCK, nRF24L01+.SCK
  N8: 3V_Itsy_Bitsy_32u4_w_Lipo_Backpack.A4, Right_Stick_COM-09032.H
  N9: 3V_Itsy_Bitsy_32u4_w_Lipo_Backpack.A3, Right_Stick_COM-09032.V
  N10: 3V_Itsy_Bitsy_32u4_w_Lipo_Backpack.A2, Left_Stick_COM-09032.H
  N11: 3V_Itsy_Bitsy_32u4_w_Lipo_Backpack.A1, Left_Stick_COM-09032.V
  +3V3: 3V_Itsy_Bitsy_32u4_w_Lipo_Backpack.+3V3, Right_Stick_COM-09032.V+, Right_Stick_COM-09032.H+, Left_Stick_COM-09032.V+, Left_Stick_COM-09032.H+, 100_uF_Capacitor_(Optional).+, nRF24L01+.VCC
  N12: Power_Switch.L1, From_Batt.pin1
  N13: Power_Switch.COM, From_Batt.pin2

notes:
  RC_Controller_V2
  by Devin Namaky 2021
  http://github.com/DrNebin
  http://www.devinnamaky.com
  +

custom parts:
  Itsy Bitsy 32u4 3V @ 8MHz: What's smaller than a Feather but larger than a Trinket? It's an Itsy Bitsy! Small, powerful, Arduino-compatible - this microcontroller board is perfect when you want something very compact, but still with a bunch of pins. Itsy Bitsy is only 1.4" long by 0.7" wide, but has 6 power pins, 6 analog & digital pins and 17 digital pins. It packs much of the same capability as an Arduino UNO or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
